# Fritzing sketch RGB_BT (saved by Fritzing 0.9.3b)
breadboards: 1

parts:
  BT1 = Bluetooth HC-06u [package=THT]
  Part1 = Arduino Uno (Rev3)
  R1 = Resistor [tolerance=±5% resistance=220 package="0603 [SMD]"]
  R2 = Resistor [tolerance=±5% resistance=220 package="0603 [SMD]"]
  R3 = Resistor [tolerance=±5% resistance=220 package="0603 [SMD]"]
  Part2 = KY-009 Full Color RGB LED SMD Module [package="Breakout board"]

nets:
  VCC: BT1.VCC, Part1.5V
  GND: BT1.GND, Part1.GND, Part2.-
  N1: BT1.TXD, Part1.D0/RX
  N2: BT1.RXD, Part1.D1/TX
  N3: Part1.D9_PWM, R1.Pin_0
  N4: Part1.D5_PWM, R2.Pin_0
  N5: Part1.D6_PWM, R3.Pin_0
  N6: R1.Pin_1, Part2.B
  N7: R2.Pin_1, Part2.G
  N8: R3.Pin_1, Part2.R

custom parts:
  Bluetooth HC-06u: Bluetooth HC-06 - face up, pins down 16.5mm x 37.5mm PCB
  KY-009 Full Color RGB LED SMD Module: RGB full color LED Module KY-009 for Arduino, emits a range of colors by mixing red, green and blue. The amount of each primary color is adjusted using PWM.

// code stored in the sketch: 01.RGB_BT.ino
/* 
 *  compatible android app https://github.com/Lukas-Heiligenbrunner/RGB-Arduino-BT-App
 *  Make sure that :
 *  
 *  You disconnect rx & tx wires when you load the program to arduino
 *  and...
 *  BT rx --> Arduino tx
 *  BT tx --> Arduino rx
 *  Have fun!
*/


#include <SoftwareSerial.h>
SoftwareSerial BLU(0,1);

int redLed = 9;           // the Red LED
int greenLed = 5;         // the green LED
int blueLed = 6;          // the blue LED

int Red = 0;
int Green = 0;
int Blue = 0;

int var;
int startstring;
int endstring;

String BT="";
String Red_string;
String Green_string;
String Blue_string;

void setup() {
    pinMode(redLed, OUTPUT);
    pinMode(greenLed, OUTPUT);
    pinMode(blueLed, OUTPUT);
    BLU.begin(9600);
}

void loop(){
    if (BLU.available()>0) {
        translateBT();
    }

}

// Function for setting RGB value
void setrgb() {
    analogWrite(redLed, Red);         // R
    analogWrite(greenLed, Green);     // G
    analogWrite(blueLed, Blue);       // B
}

void translateBT() {                // user written function, action based on BT signal received
  while (BLU.available()) {         
    delay(1);
    BT += (char)BLU.read();
  }

  if ( BT.length() <= 11 ) {       // check if string is in range of xxx/xxx/xxx 11 characters
    startstring=0;
    endstring = 1;
    for ( var=0; var <= (int)BT.length() ; var++ ) {
      if ( BT.charAt(var) == '/' ) {
        if ( endstring == 1 ) {
          Red_string = BT.substring(startstring, var);
        }
        else if ( endstring == 2 ) {
          Green_string = BT.substring(startstring + 1, var);
          Blue_string = BT.substring(var + 1, BT.length());
        }
        startstring = var;
        endstring = endstring + 1;
      }
      else {
        Red = 0;
        Green = 0;
        Blue = 0;
        setrgb();
      }
    }

  Red = Red_string.toInt();
  Green = Green_string.toInt();
  Blue = Blue_string.toInt();
  setrgb();
  BT="";
  BLU.end();          // Flush serial communication
  BLU.begin(9600);    // Restart a fresh serial
  }
  else {
    Red = 0;
    Green = 0;
    Blue = 0;
    setrgb();
  }
}

// code stored in the sketch: 01.RGB_REMOTE.ino
#include <IRremote.h>
#include <Wire.h> 
#include <LiquidCrystal_I2C.h>
#include <SoftwareSerial.h>
SoftwareSerial BLU(0,1);
LiquidCrystal_I2C lcd(0x27,16,2);  // set the LCD address to 0x27 for a 16 chars and 2 line display


int redLed = 9;           // the Red LED
int greenLed = 5;         // the green LED
int blueLed = 6;          // the blue LED
int receiver = 11;        // pin 11 IR receiver
int Red = 0;
int Green = 0;
int Blue = 0;
long irCode;
int var;
int startstring;
int endstring;
String BT="";
String Red_string;
String Green_string;
String Blue_string;


IRrecv irrecv(receiver);           // create instance of 'irrecv'
decode_results results;            // create instance of 'decode_results'

void setup() {
  pinMode(redLed, OUTPUT);
  pinMode(greenLed, OUTPUT);
  pinMode(blueLed, OUTPUT);
  irrecv.enableIRIn(); // Start the receiver
  lcd.init();
  lcd.backlight();
  lcd.setCursor(0,0);
  lcd.print("RGB LED Project");
  lcd.setCursor(0,1);
  lcd.print("2017");
  Serial.begin(9600);
  BLU.begin(9600);
}

void loop(){

  if (irrecv.decode(&results)) {            // have we received an IR signal?
    if (results.value == 0xFFFFFFFF) {      // check if long press
      results.value = irCode;
    }
    translateIR();                    // user written funtion for IR comm
    irrecv.resume();                  // receive next value
    setrgb();
  }

  if (BLU.available()>0) {            // compatible android app https://github.com/Lukas-Heiligenbrunner/RGB-Arduino-BT-App
    translateBT();
  }

}

// Function for setting RGB value
void setrgb() {
  analogWrite(redLed, Red);         // R
  analogWrite(greenLed, Green);     // G
  analogWrite(blueLed, Blue);       // B
}


void translateBT() {                // user written function, action based on BT signal received
  while (BLU.available()) {         // compatible android app https://github.com/Lukas-Heiligenbrunner/RGB-Arduino-BT-App
    delay(1);
    BT += (char)BLU.read();
  }

  if ( BT.length() <= 11 ) {       // check if string is in range of xxx/xxx/xxx 11 characters
    startstring=0;
    endstring = 1;
    for ( var=0; var <= (int)BT.length() ; var++ ) {
      if ( BT.charAt(var) == '/' ) {
        if ( endstring == 1 ) {
          Red_string = BT.substring(startstring, var);
        }
        else if ( endstring == 2 ) {
          Green_string = BT.substring(startstring + 1, var);
          Blue_string = BT.substring(var + 1, BT.length());
        }
        startstring = var;
        endstring = endstring + 1;
      }
      else {
        Red = 0;
        Green = 0;
        Blue = 0;
        setrgb();
      }
    }

  Red = Red_string.toInt();
  Green = Green_string.toInt();
  Blue = Blue_string.toInt();
  setrgb();
  lcd.clear();
  lcd.setCursor(0, 0);
  lcd.print("Via BT R:" + Red_string);
  lcd.setCursor(0, 1);
  lcd.print(" G:" + Green_string + " B:" + Blue_string);
  BT="";
  Serial.end();
  BLU.end();
  Serial.begin(9600);
  BLU.begin(9600);
  }
  else {
    Red = 0;
    Green = 0;
    Blue = 0;
    setrgb();
  }
}

void translateIR() {                 // user written funtion, action based on IR code received
  
  switch(results.value) {
  
  case 5316027:                       // decimal value old 0x977A8DEA 
  lcd.clear();  
  lcd.print(" ON/OFF ");  
  if (Red == 0 && Blue == 0 && Green == 0) {
    Red = 255;
    Green = 255;
    Blue = 255;
  }
  else {
    Red = 0;
    Green = 0;
    Blue = 0;
  }
  irCode = 5316027;                   // hex value
  break;
  
  case 0xF076C13B:                    // hex value
  lcd.clear();
  lcd.print(" Bright - ");
  if (Red > 5) {
    Red = Red - 5;
  }
  else {
    Red = 0;
  }
  if (Green > 5) {
    Green = Green - 5;
  }
  else {
    Green = 0;
  }
  if (Blue > 5) {
    Blue = Blue - 5;
  }
  else {
    Blue = 0;
  }
  lcd.setCursor(0, 1);
  lcd.print(Red + " ");
  lcd.print(Green + " ");
  lcd.print(Blue + " ");
  irCode = 4034314555;              // decimal value
  break;

  case 0xA3C8EDDB:  
  lcd.clear();
  lcd.setCursor(0, 0);
  lcd.print(" Bright + "); 
  if (Red < 250) {
    Red = Red + 5;
  }
  else {
    Red = 255;
  }
  if (Green < 250) {
    Green = Green + 5;
  }
  else {
    Green = 255;
  }
  if (Blue < 250) {
    Blue = Blue + 5;
  }
  else {
    Blue = 255;
  }
  lcd.setCursor(0, 1);
  lcd.print(Red);
  lcd.print(Green);
  lcd.print(Blue);
  irCode = 2747854299;
  break;

  case 0x9716BE3F:
  lcd.clear();
  lcd.setCursor(0, 0);
  lcd.print("Red");
  Red = 255;
  Green = 0;
  Blue = 0;
  irCode = 0x9716BE3F;
  break;

  case 0x3D9AE3F7:
  lcd.clear();
  lcd.setCursor(0, 0);
  lcd.println("Green");
  Red = 0;
  Green = 255;
  Blue = 0;
  irCode = 0x3D9AE3F7;
  break;

  case 0x6182021B:
  lcd.clear();
  lcd.setCursor(0, 0);
  lcd.print("Blue");
  Red = 0;
  Green = 0;
  Blue = 255;
  irCode = 0x6182021B;
  break;

  case 0x32C6FDF7:
  lcd. clear();
  lcd.setCursor(0, 0);
  lcd.print("Red bright -  ");
  if (Red > 5) {
    Red = Red - 5;
  }
  else {
    Red = 0;
  }
  lcd.setCursor(0, 1);
  lcd.print(Red);
  irCode = 0x32C6FDF7;
  break;

  case 0x8C22657B:
  lcd.clear();
  lcd.setCursor(0, 0);
  lcd.print("Red bright +  ");
  if (Red < 250) {
    Red = Red + 5;
  }
  else {
    Red = 255;
  }
  lcd.setCursor(0, 1);
  lcd.print(Red);
  irCode = 0x8C22657B;
  break;

  case 0x1BC0157B:
  lcd.clear();
  lcd.setCursor(0, 0);
  lcd.print("Green bright -  ");
  if (Green > 5) {
    Green = Green - 5;
  }
  else {
    Green = 0;
  }
  lcd.setCursor(0, 1);
  lcd.print(Green);
  irCode = 0x1BC0157B;
  break;

  case 0x488F3CBB:
  lcd.clear();
  lcd.setCursor(0, 0);
  lcd.print("Green bright +  ");
  if (Green < 250) {
    Green = Green + 5;
  }
  else {
    Green = 255;
  }
  lcd.setCursor(0, 1);
  lcd.print(Green);
  irCode = 0x488F3CBB;
  break;

  case 0x3EC3FC1B:
  lcd.clear();
  lcd.setCursor(0, 0);
  lcd.print("Blue bright -  ");
  if (Blue > 5) {
    Blue = Blue - 5;
  }
  else {
    Blue = 0;
  }
  lcd.setCursor(0, 1);
  lcd.print(Blue);
  irCode = 0x3EC3FC1B;
  break;

  case 0x449E79F:
  lcd.clear();
  lcd.setCursor(0, 0);
  lcd.print("Blue bright +  ");
  if (Blue < 250) {
  Blue = Blue + 5;
  }
  else {
    Blue = 255;
  }
  lcd.setCursor(0, 1);
  lcd.print(Blue);
  irCode = 0x449E79F;
  break;

  case 0x20FE4DBB:
  lcd.clear();
  lcd.setCursor(0, 0);
  lcd.print("Program mode ");
  policestrobe();
  fader();
  crossfade();
  irCode = 0x20FE4DBB;
  break;

  default: 
  lcd.clear();
  lcd.setCursor(0, 0);  
  lcd.print(results.value, HEX);
  break;
  }
}

// random play...

void policestrobe() {
  analogWrite(redLed, 0);
  analogWrite(greenLed, 0);
  analogWrite(blueLed, 0);

    for (var = 0; var < 10; var++) {
    analogWrite(redLed, 255);
    delay(100);
    analogWrite(redLed, 0);
    delay(100);
    }
    for (var = 0; var < 10; var++) {
    analogWrite(blueLed, 255);
    delay(100);
    analogWrite(blueLed, 0);
    delay(100);
    }
    for (var = 0; var < 10; var++) {
    analogWrite(redLed, 255);
    delay(150);
    analogWrite(redLed, 0);
    analogWrite(blueLed, 255);
    delay(150);
    analogWrite(blueLed, 0);
    }
}

void fader() {
  analogWrite(redLed, 0);
  analogWrite(greenLed, 0);
  analogWrite(blueLed, 0);
    for (var = 0; var <= 255; var++) {
      analogWrite(redLed, var);
      delay(20);
    }
  analogWrite(redLed, 0);
  analogWrite(greenLed,255);
    for (var = 255; var >= 0; var--) {
      analogWrite(greenLed, var);
      delay(20);
    }
    for (var = 0; var <= 255; var++) {
      analogWrite(blueLed, var);
      delay(20);
    }
  analogWrite(blueLed, 0);
}

void crossfade() {
  analogWrite(redLed, 0);
  analogWrite(greenLed, 0);
  analogWrite(blueLed, 0);
    for (var = 0; var <= 255; var++) {
      analogWrite(redLed, var);
      analogWrite(greenLed, 255-var);
      delay(20);
    }
    for (var = 0; var <= 255; var++) {
      analogWrite(redLed, 255-var);
      analogWrite(blueLed, var);
      delay(20);
    }
    for (var = 0; var <= 255; var++) {
      analogWrite(blueLed, 255-var);
      analogWrite(greenLed, var);
      delay(20);
    }
}
